// Logisim project C208Aula.circ as structural Verilog
module MeioSomador (
  input  in_1,
  input  in_2,
  output out_3,
  output out_4
);

  xor xor_1 (out_3, in_1, in_2);
  and and_1 (out_4, in_1, in_2);
endmodule

module SomadorCompleto (
  input  in_1,
  input  in_2,
  input  in_3,
  output out_4,
  output out_5
);

  wire cout_out_3, cout_out_4, meiosomador_1_out_4;

  MeioSomador cout (.out_4(cout_out_4), .out_3(cout_out_3));  // open: in_2, in_1
  MeioSomador meiosomador_1 (.out_4(meiosomador_1_out_4), .out_3(out_4));  // open: in_2, in_1
  or or_1 (out_5, meiosomador_1_out_4, cout_out_4);
endmodule

module MeioSubtrator (
  input  in_1,
  input  in_2,
  output out_3,
  output out_4
);

  wire not_1_out;

  not not_1 (not_1_out, in_1);
  xor xor_1 (out_3, in_1, in_2);
  and and_1 (out_4, in_2, not_1_out);
endmodule

module SubtratorCompleto (
  input  in_1,
  input  in_2,
  input  in_3,
  output out_4,
  output out_5
);

  wire meiosubtrator_1_out_3, meiosubtrator_1_out_4, meiosubtrator_2_out_4;

  MeioSubtrator meiosubtrator_1 (.out_3(meiosubtrator_1_out_3), .out_4(meiosubtrator_1_out_4));  // open: in_2, in_1
  MeioSubtrator meiosubtrator_2 (.out_3(out_4), .out_4(meiosubtrator_2_out_4));  // open: in_2, in_1
  or or_1 (out_5, meiosubtrator_2_out_4, meiosubtrator_1_out_4);
endmodule

module Exercicio1 (
  input  [1:0] in_1,
  input  in_2,
  output [1:0] out_3
);

  wire [1:0] demultiplexer_1_out0, demultiplexer_1_out1, meiosomador_1_out_3, meiosubtrator_1_out_3;

  Demultiplexer #(.width(2), .enable("false")) demultiplexer_1 (
    .out0(demultiplexer_1_out0), .out1(demultiplexer_1_out1), .in(in_1), .sel(in_2));
  MeioSomador meiosomador_1 (.out_4(meiosomador_1_out_3[1]), .out_3(meiosomador_1_out_3[0]));  // open: in_2, in_1
  MeioSubtrator meiosubtrator_1 (
    .out_3(meiosubtrator_1_out_3[0]), .out_4(meiosubtrator_1_out_3[1]));  // open: in_2, in_1
  Multiplexer #(.width(2), .enable("false")) multiplexer_1 (
    .in0(meiosomador_1_out_3), .in1(meiosubtrator_1_out_3), .out(out_3), .sel(in_2));

  // Notes on the sheet:
  //   Meio Subtrator
endmodule

module Exercicio2 (
  input  [2:0] in_1,
  input  in_2,
  output [1:0] out_3
);

  wire [1:0] somadorcompleto_1_out_4, subtratorcompleto_1_out_4;
  wire [2:0] demultiplexer_1_out0, demultiplexer_1_out1;

  Demultiplexer #(.width(3), .enable("false")) demultiplexer_1 (
    .out0(demultiplexer_1_out0), .out1(demultiplexer_1_out1), .in(in_1), .sel(in_2));
  SubtratorCompleto subtratorcompleto_1 (
    .out_4(subtratorcompleto_1_out_4[0]), .in_2(demultiplexer_1_out1[1]), .in_3(demultiplexer_1_out1[2]),
    .out_5(subtratorcompleto_1_out_4[1]), .in_1(demultiplexer_1_out1[0]));
  SomadorCompleto somadorcompleto_1 (
    .out_4(somadorcompleto_1_out_4[0]), .out_5(somadorcompleto_1_out_4[1]));  // open: in_2, in_3, in_1
  Multiplexer #(.width(2), .enable("false")) multiplexer_1 (
    .in0(somadorcompleto_1_out_4), .in1(subtratorcompleto_1_out_4), .out(out_3), .sel(in_2));
endmodule

module Complemento2 (
  input  [3:0] in_1,
  input  [3:0] in_2,
  input  in_3,
  input  [3:0] in_4,
  output out_5
);

  wire multiplexer_1_out, multiplexer_2_out, multiplexer_3_out, multiplexer_4_out, not_1_out, not_2_out,
       not_3_out, not_4_out, somadorcompleto_2_out_5, somadorcompleto_3_out_5, somadorcompleto_4_out_5;

  not not_1 (not_1_out, in_2[3]);
  Multiplexer #(.enable("false")) multiplexer_1 (.in0(in_2[3]), .in1(not_1_out), .out(multiplexer_1_out), .sel(in_3));
  SomadorCompleto somadorcompleto_1 (
    .out_4(in_4[0]), .in_2(in_1[3]), .in_3(multiplexer_1_out), .out_5(out_5), .in_1(somadorcompleto_2_out_5));
  not not_2 (not_2_out, in_2[2]);
  Multiplexer #(.enable("false")) multiplexer_2 (.in0(in_2[2]), .in1(not_2_out), .out(multiplexer_2_out), .sel(in_3));
  SomadorCompleto somadorcompleto_2 (
    .out_4(in_4[1]), .in_2(in_1[2]), .in_3(multiplexer_2_out), .out_5(somadorcompleto_2_out_5),
    .in_1(somadorcompleto_3_out_5));
  not not_3 (not_3_out, in_2[1]);
  Multiplexer #(.enable("false")) multiplexer_3 (.in0(in_2[1]), .in1(not_3_out), .out(multiplexer_3_out), .sel(in_3));
  SomadorCompleto somadorcompleto_3 (
    .out_4(in_4[2]), .in_2(in_1[1]), .in_3(multiplexer_3_out), .out_5(somadorcompleto_3_out_5),
    .in_1(somadorcompleto_4_out_5));
  not not_4 (not_4_out, in_2[0]);
  Multiplexer #(.enable("false")) multiplexer_4 (.in0(in_2[0]), .in1(not_4_out), .out(multiplexer_4_out), .sel(in_3));
  SomadorCompleto somadorcompleto_4 (
    .out_4(in_4[3]), .in_2(in_1[0]), .in_3(multiplexer_4_out), .out_5(somadorcompleto_4_out_5), .in_1(in_3));
endmodule

module Multiplicacao (
  input  in_1,
  input  in_2,
  input  in_3,
  input  in_4,
  output out_5,
  output out_6,
  output out_7
);

  wire and_1_out, and_2_out, and_3_out, meiosomador_2_out_4;

  and and_1 (and_1_out, in_1, in_3);
  and and_2 (and_2_out, in_1, in_4);
  MeioSomador meiosomador_1 (.out_4(out_5), .in_2(and_1_out), .out_3(out_6), .in_1(meiosomador_2_out_4));
  and and_3 (and_3_out, in_2, in_3);
  // AND_Gate and_4 has open pins: in0=in_2, in1=in_4, out=open
  MeioSomador meiosomador_2 (.out_4(meiosomador_2_out_4), .in_2(and_2_out), .out_3(out_7), .in_1(and_3_out));
endmodule

module RegistradorCargaParalela (
  input  [3:0] in_1,
  input  [3:0] in_2,
  input  in_3,
  input  in_4,
  input  in_5
);

  wire multiplexer_1_out, multiplexer_2_out, multiplexer_3_out, multiplexer_4_out;

  D_Flip_Flop d_ff_1 (.D(multiplexer_1_out), .clk(in_3), .Q(in_2[3]), .reset(in_5));  // open: Qn, preset
  Multiplexer #(.enable("false")) multiplexer_1 (.in0(in_2[3]), .in1(in_1[0]), .out(multiplexer_1_out), .sel(in_4));
  D_Flip_Flop d_ff_2 (.D(multiplexer_2_out), .clk(in_3), .Q(in_2[2]), .reset(in_5));  // open: Qn, preset
  Multiplexer #(.enable("false")) multiplexer_2 (.in0(in_2[2]), .in1(in_1[1]), .out(multiplexer_2_out), .sel(in_4));
  D_Flip_Flop d_ff_3 (.D(multiplexer_3_out), .clk(in_3), .Q(in_2[1]), .reset(in_5));  // open: Qn, preset
  Multiplexer #(.enable("false")) multiplexer_3 (.in0(in_2[1]), .in1(in_1[2]), .out(multiplexer_3_out), .sel(in_4));
  D_Flip_Flop d_ff_4 (.D(multiplexer_4_out), .clk(in_3), .Q(in_2[0]), .reset(in_5));  // open: Qn, preset
  Multiplexer #(.enable("false")) multiplexer_4 (.in0(in_2[0]), .in1(in_1[3]), .out(multiplexer_4_out), .sel(in_4));
endmodule
