// Logisim project circuit1.circ as structural Verilog: 1 circuit, main circuit main
module main (
  input  in_1,
  input  in_2,
  input  [3:0] in_3,
  input  in_4,
  input  in_5
);

  wire ALU_SRC, and_2_out, CLOCK, REG_W, registerfile_1_p6;
  wire [4:0] multiplexer_1_out;
  wire [5:0] OPCODE;
  wire [25:0] mipsprogramrom_1_p2;
  wire [31:0] adder_1_out, bit_extender_1_out, mips_alu_1_p4, mips_ram_1_p7, multiplexer_2_out, register_1_q,
       registerfile_1_p7;

  Clock clock_1 (.out(CLOCK));
  Adder #(.width(32)) adder_1 (.a(register_1_q), .b(32'h4), .out(adder_1_out));  // open: cin, cout
  and and_1 (ALU_SRC, ~OPCODE[0], OPCODE[1], OPCODE[2], ~OPCODE[3], OPCODE[4], OPCODE[5]);  // AND_Gate
  and and_2 (and_2_out, OPCODE[0], OPCODE[1], OPCODE[2], OPCODE[4], OPCODE[5]);
  Register #(.width(32)) register_1 (.D(adder_1_out), .clk(CLOCK), .Q(register_1_q));  // open: en, clr
  or or_1 (REG_W, ALU_SRC, and_2_out);
  // MIPSProgramROM mipsprogramrom_1: pin names not known; wires that end beside it: register_1_q, {OPCODE, mipsprogramrom_1_p2}
  Multiplexer #(.width(5), .enable("false")) multiplexer_1 (
    .in0(mipsprogramrom_1_p2[15:11]), .in1(mipsprogramrom_1_p2[20:16]), .out(multiplexer_1_out), .sel(ALU_SRC));
  // RegisterFile registerfile_1: pin names not known; wires that end beside it: CLOCK, REG_W, multiplexer_1_out, mipsprogramrom_1_p2[25:21], mipsprogramrom_1_p2[20:16], registerfile_1_p6, registerfile_1_p7
  assign bit_extender_1_out = {{16{mipsprogramrom_1_p2[15]}}, mipsprogramrom_1_p2[15:0]};  // Bit_Extender bit_extender_1
  Multiplexer #(.width(32), .enable("false")) multiplexer_2 (
    .in0(registerfile_1_p7), .in1(bit_extender_1_out), .out(multiplexer_2_out), .sel(ALU_SRC));
  // Mips_ALU mips_alu_1: pin names not known; wires that end beside it: registerfile_1_p6, multiplexer_2_out, in_3, mips_alu_1_p4
  // MIPS_RAM mips_ram_1: pin names not known; wires that end beside it: mips_alu_1_p4[19:0], registerfile_1_p7, in_2, CLOCK, in_4, in_5, mips_ram_1_p7
  Multiplexer #(.width(32), .enable("false")) multiplexer_3 (
    .in0(mips_alu_1_p4), .in1(mips_ram_1_p7), .sel(in_1));  // open: out

  // Other names for the same wires on the sheet: REG_DEST = ALU_SRC

  // Notes on the sheet:
  //   contents of mipsprogramrom_1 (hex, n*v repeats v):
  //   addiu $2, $0, 0x0020 addu $3, $1, $2
endmodule
