// Logisim project projeto2_final_isaque_samuel.circ as structural Verilog: 2 circuits, main circuit main
module main (
  input  in_1,
  input  in_2,
  output [5:0] FUNCT,
  output [4:0] SHIFT_AMOUNT,
  output [4:0] R_DESTINO,
  output [5:0] OPCODE
);

  wire ALU_SRC, CLK, REG_WRITE, registerfile_1_p7;
  wire [3:1] ALU_OP;
  wire [4:0] multiplexer_1_out;
  wire [25:16] mipsprogramrom_1_p2;
  wire [31:0] adder_1_out, bit_extender_1_out, mips_alu_1_p4, mips_ram_1_p6, mipsprogramrom_1_p1,
       multiplexer_2_out, registerfile_1_p2, registerfile_1_p8;

  Adder #(.width(32)) adder_1 (.a(mipsprogramrom_1_p1), .b(32'h4), .out(adder_1_out));  // open: cin, cout
  // MIPSProgramROM mipsprogramrom_1: pin names not known; wires that end beside it: mipsprogramrom_1_p1, {OPCODE, mipsprogramrom_1_p2, R_DESTINO, SHIFT_AMOUNT, FUNCT}
  Register #(.width(32)) PC (.D(adder_1_out), .clk(CLK), .Q(mipsprogramrom_1_p1));  // open: en, clr
  Multiplexer #(.width(5), .enable("false")) multiplexer_1 (
    .in0(R_DESTINO), .in1(mipsprogramrom_1_p2[20:16]), .out(multiplexer_1_out), .sel(ALU_SRC));
  and ADDIU (ALU_SRC, OPCODE[0], ~OPCODE[1], ~OPCODE[2], OPCODE[3], ~OPCODE[4], ~OPCODE[5]);  // AND_Gate
  // AND_Gate R_TYPE has open pins: in0=OPCODE[0], in1=OPCODE[1], in2=OPCODE[2], in3=OPCODE[3], in4=OPCODE[4], in5=OPCODE[5], out=open
  // AND_Gate ADD has open pins: in0=FUNCT[0], in1=FUNCT[1], in2=FUNCT[2], in3=FUNCT[3], in4=FUNCT[4], in5=FUNCT[5], out=open
  and AND_OP (ALU_OP[3], ~FUNCT[0], ~FUNCT[1], FUNCT[2], ~FUNCT[3], ~FUNCT[4], FUNCT[5]);  // AND_Gate
  assign bit_extender_1_out = {{16{R_DESTINO[4]}}, {R_DESTINO, SHIFT_AMOUNT, FUNCT}};  // Bit_Extender bit_extender_1
  Clock clock_1 (.out(CLK));
  not not_1 (REG_WRITE, in_1);
  not not_2 (ALU_OP[1], in_2);
  // RegisterFile registerfile_1: pin names not known; wires that end beside it: CLK, registerfile_1_p2, REG_WRITE, multiplexer_1_out, mipsprogramrom_1_p2[25:21], mipsprogramrom_1_p2[20:16], registerfile_1_p7, registerfile_1_p8
  Multiplexer #(.width(32), .enable("false")) multiplexer_2 (
    .in0(registerfile_1_p8), .in1(bit_extender_1_out), .out(multiplexer_2_out), .sel(ALU_SRC));
  // Mips_ALU mips_alu_1: pin names not known; wires that end beside it: registerfile_1_p7, multiplexer_2_out, {ALU_OP[3], in_2, ALU_OP[1], in_2}, mips_alu_1_p4
  // MIPS_RAM mips_ram_1: pin names not known; wires that end beside it: mips_alu_1_p4[19:0], registerfile_1_p8, in_1, CLK, in_1, mips_ram_1_p6
  Multiplexer #(.width(32), .enable("false")) multiplexer_3 (
    .in0(mips_alu_1_p4), .in1(mips_ram_1_p6), .out(registerfile_1_p2), .sel(in_1));

  // Other names for the same wires on the sheet: ALU_OP (some bits) = {2{in_2}}; SELECT_REG_DEST = ALU_SRC;
  //   LOAD = in_1; MEM_TO_REG = in_1; STORE = in_1

  // Notes on the sheet:
  //   MEMORIA DE PROGRAMA
  //   CONTA DE 4 EM 4, A CADA INSTRUÇÃO
  //   contents of mipsprogramrom_1 (hex, n*v repeats v):
  //   addiu $t2,$t0,0xC addiu $t1,$t1,0xA addiu $t2,$t2,0xC addu $t3,$t1,$t2 addiu $t4,$t0,0x28 and
  //   $t5,$t3,$t4
  //   INSTRUCTION DECODE
  //   R
  //   I
  //   IMMEDIATE VALUE (16 BITS)
  //   REGISTRADOR 1
  //   REGISTRADOR 2 (TIPO R)
  //   REGISTRADOR DE DESTINO
  //   DADO A SER GRAVADO
  //   BANCO DE REGISTRADORES
  //   REG1_OUT
  //   REG2_OUT
  //   ENDERECO BASE(LOAD/STORE)
  //   OFFSET(LOAD/STORE)
  //   2^20 ENDEREÇOS
  //   OPERACOES SEM UTILIZAR MEMORIA
  //   MEMORIA DE DADOS (RAM)
  //   LOAD
endmodule

module teste (
);

  wire [31:0] mipsprogramrom_1_p2;

  // MIPSProgramROM mipsprogramrom_1: pin names not known; wires that end beside it: {32{1'b0}}, mipsprogramrom_1_p2
endmodule
