// Logisim project CAMINHO_04_Turma_b_SIMPLIFICADO.circ as structural Verilog: 1 circuit, main circuit main
module main (
  input  [3:0] in_1,
  input  in_2
);

  wire and_2_out, CLK, LOAD, REG_W, registerfile_1_p7, STORE;
  wire [4:0] multiplexer_1_out;
  wire [31:0] adder_1_out, bit_extender_1_out, mips_alu_1_p4, mips_ram_1_p6, mipsprogramrom_1_p2,
       multiplexer_2_out, register_1_q, registerfile_1_p1, registerfile_1_p8;

  Adder #(.width(32)) adder_1 (.a(register_1_q), .b(32'h4), .out(adder_1_out));  // open: cin, cout
  Register #(.width(32)) register_1 (.D(adder_1_out), .Q(register_1_q), .clk(CLK));  // open: en, clr
  // MIPSProgramROM mipsprogramrom_1: pin names not known; wires that end beside it: register_1_q, mipsprogramrom_1_p2
  Multiplexer #(.width(5)) multiplexer_1 (
    .in0(mipsprogramrom_1_p2[15:11]), .in1(mipsprogramrom_1_p2[20:16]), .out(multiplexer_1_out), .sel(in_2));  // open: en
  assign bit_extender_1_out = {{16{mipsprogramrom_1_p2[15]}}, mipsprogramrom_1_p2[15:0]};  // Bit_Extender bit_extender_1
  and and_1 (LOAD, mipsprogramrom_1_p2[26], mipsprogramrom_1_p2[27], mipsprogramrom_1_p2[31]);
  and and_2 (and_2_out, mipsprogramrom_1_p2[26], mipsprogramrom_1_p2[29]);
  and and_3 (STORE, LOAD, mipsprogramrom_1_p2[29]);
  or or_1 (REG_W, and_2_out, LOAD);
  // RegisterFile registerfile_1: pin names not known; wires that end beside it: registerfile_1_p1, CLK, REG_W, multiplexer_1_out, mipsprogramrom_1_p2[25:21], mipsprogramrom_1_p2[20:16], registerfile_1_p7, registerfile_1_p8
  Clock clock_1 (.out(CLK));
  Multiplexer #(.width(32)) multiplexer_2 (
    .in0(registerfile_1_p8), .in1(bit_extender_1_out), .out(multiplexer_2_out), .sel(in_2));  // open: en
  // Mips_ALU mips_alu_1: pin names not known; wires that end beside it: registerfile_1_p7, multiplexer_2_out, in_1, mips_alu_1_p4
  // MIPS_RAM mips_ram_1: pin names not known; wires that end beside it: mips_alu_1_p4[19:0], registerfile_1_p8, STORE, CLK, LOAD, mips_ram_1_p6
  Multiplexer #(.width(32)) multiplexer_3 (
    .in0(mips_alu_1_p4), .in1(mips_ram_1_p6), .out(registerfile_1_p1), .sel(LOAD));  // open: en

  // Other names for the same wires on the sheet: MEM_TO_REG = LOAD; ALU_SRC = in_2; REG_DEST = in_2

  // Notes on the sheet:
  //   MEMÓRIA DE PROGRAMA
  //   contents of mipsprogramrom_1 (hex, n*v repeats v):
  //   addiu $2,$0,0x50 addiu $3,$0,0x80 sw $1,4($3) lw $4,4($3)
  //   OPCODE
  //   R
  //   I
  //   VAZIO
  //   VAZIO
endmodule
