// Logisim project teste.circ as structural Verilog: 2 circuits, main circuit main
module main (
  input  [3:0] ALU_OP,
  output [5:0] FUNCT,
  output [4:0] SHIFT_AMOUNT,
  output [4:0] R_DESTINO,
  output [5:0] OPCODE
);

  wire ALU_SRC, and_1_out, and_2_out, CLK, LOAD, REG_WRITE, registerfile_1_p7, STORE;
  wire [4:0] multiplexer_1_out;
  wire [25:16] mipsprogramrom_1_p2;
  wire [31:0] adder_1_out, bit_extender_1_out, mips_alu_1_p4, mips_ram_1_p6, mipsprogramrom_1_p1,
       multiplexer_2_out, registerfile_1_p2, registerfile_1_p8;

  Adder #(.width(32)) adder_1 (.a(mipsprogramrom_1_p1), .b(32'h4), .out(adder_1_out));  // open: cin, cout
  // MIPSProgramROM mipsprogramrom_1: pin names not known; wires that end beside it: mipsprogramrom_1_p1, {OPCODE, mipsprogramrom_1_p2, R_DESTINO, SHIFT_AMOUNT, FUNCT}
  Register #(.width(32)) register_1 (.D(adder_1_out), .clk(CLK), .Q(mipsprogramrom_1_p1));  // open: en, clr
  Multiplexer #(.width(5), .enable("false")) multiplexer_1 (
    .in0(R_DESTINO), .in1(mipsprogramrom_1_p2[20:16]), .out(multiplexer_1_out), .sel(ALU_SRC));
  and and_1 (and_1_out, ~OPCODE[0], ~OPCODE[1], ~OPCODE[2], ~OPCODE[3], ~OPCODE[4], ~OPCODE[5]);  // AND_Gate
  and and_2 (and_2_out, OPCODE[0], ~OPCODE[1], ~OPCODE[2], OPCODE[3], ~OPCODE[4], ~OPCODE[5]);  // AND_Gate
  and and_3 (LOAD, OPCODE[0], OPCODE[1], ~OPCODE[2], ~OPCODE[3], ~OPCODE[4], OPCODE[5]);  // AND_Gate
  and and_4 (STORE, OPCODE[0], OPCODE[1], ~OPCODE[2], OPCODE[3], ~OPCODE[4], OPCODE[5]);  // AND_Gate
  assign bit_extender_1_out = {{16{R_DESTINO[4]}}, {R_DESTINO, SHIFT_AMOUNT, FUNCT}};  // Bit_Extender bit_extender_1
  or or_1 (ALU_SRC, and_2_out, LOAD, STORE);
  or or_2 (REG_WRITE, and_1_out, and_2_out, LOAD);
  // RegisterFile registerfile_1: pin names not known; wires that end beside it: CLK, registerfile_1_p2, REG_WRITE, multiplexer_1_out, mipsprogramrom_1_p2[25:21], mipsprogramrom_1_p2[20:16], registerfile_1_p7, registerfile_1_p8
  Clock clock_1 (.out(CLK));
  Multiplexer #(.width(32), .enable("false")) multiplexer_2 (
    .in0(registerfile_1_p8), .in1(bit_extender_1_out), .out(multiplexer_2_out), .sel(ALU_SRC));
  // Mips_ALU mips_alu_1: pin names not known; wires that end beside it: registerfile_1_p7, multiplexer_2_out, ALU_OP, mips_alu_1_p4
  // MIPS_RAM mips_ram_1: pin names not known; wires that end beside it: mips_alu_1_p4[19:0], registerfile_1_p8, STORE, CLK, LOAD, mips_ram_1_p6
  Multiplexer #(.width(32), .enable("false")) multiplexer_3 (
    .in0(mips_alu_1_p4), .in1(mips_ram_1_p6), .out(registerfile_1_p2), .sel(LOAD));

  // Other names for the same wires on the sheet: MEM_TO_REG = LOAD; SELECT_REG_DEST = ALU_SRC

  // Notes on the sheet:
  //   MEMORIA DE PROGRAMA
  //   contents of mipsprogramrom_1 (hex, n*v repeats v):
  //   addiu $2, $0, 0x50 addiu $3, $0, 0x80 sw $1, 4($3) lw $4, 4($3)
  //   ADDIU
  //   LW
  //   SW
  //   R
  //   I
  //   ADDU
  //   DADO A SER GRAVADO
  //   BANCO DE REGISTRADORES
  //   REG1_OUT
  //   REG2_OUT
  //   ENDERECO BASE
  //   OFFSET
  //   OPERACOES SEM UTILIZAR MEMORIA
  //   MEMORIA DE DADOS (RAM)
  //   LOAD
endmodule

module teste (
);

  wire [31:0] mipsprogramrom_1_p2;

  // MIPSProgramROM mipsprogramrom_1: pin names not known; wires that end beside it: {32{1'b0}}, mipsprogramrom_1_p2
endmodule
